// Logisim project Adder.circ as structural Verilog: 6 circuits, main circuit main
module main (
  input  A0,
  input  B0,
  input  A1,
  input  B1,
  input  A2,
  input  B2,
  output out_7
);

  wire decoderr_1_a_2, decoderr_1_b_2, decoderr_1_c_2, decoderr_1_d, decoderr_1_e, decoderr_1_f,
       decoderr_1_g, registrador_1_out_5, registrador_1_out_6, registrador_1_out_7, somador_1_c,
       somador_1_s0, somador_1_s1, somador_1_s2;

  Somador somador_1 (
    .A0(A0), .B0(B0), .A1(A1), .B1(B1), .A2(A2), .B2(B2), .S0(somador_1_s0), .S1(somador_1_s1),
    .S2(somador_1_s2), .C(somador_1_c));
  Registrador registrador_1 (
    .in_1(somador_1_s0), .in_2(somador_1_s1), .in_3(somador_1_s2), .in_4(somador_1_c),
    .out_5(registrador_1_out_5), .out_6(registrador_1_out_6), .out_7(registrador_1_out_7), .out_8(out_7));
  Decoderr decoderr_1 (
    .C(registrador_1_out_7), .B(registrador_1_out_6), .A(registrador_1_out_5), .a_2(decoderr_1_a_2),
    .b_2(decoderr_1_b_2), .c_2(decoderr_1_c_2), .d(decoderr_1_d), .e(decoderr_1_e), .f(decoderr_1_f),
    .g(decoderr_1_g));
  _7_Segment_Display u_7_segment_display_1 (
    .g(decoderr_1_g), .f(decoderr_1_f), .a(decoderr_1_a_2), .b(decoderr_1_b_2), .e(decoderr_1_e),
    .d(decoderr_1_d), .c(decoderr_1_c_2));  // open: dp
endmodule

module Carry (
  input  in_1,
  input  in_2,
  output S,
  output C
);

  and and_1 (C, in_2, in_1);
  xor xor_1 (S, in_1, in_2);
endmodule

module Registrador (
  input  in_1,
  input  in_2,
  input  in_3,
  input  in_4,
  output out_5,
  output out_6,
  output out_7,
  output out_8
);

  wire clock_1_out;

  Clock clock_1 (.out(clock_1_out));
  D_Flip_Flop d_ff_1 (.clk(clock_1_out), .D(in_3), .Q(out_7));  // open: Qn, preset, en, reset
  D_Flip_Flop d_ff_2 (.clk(clock_1_out), .D(in_4), .Q(out_8));  // open: Qn, preset, en, reset
  D_Flip_Flop d_ff_3 (.clk(clock_1_out), .D(in_2), .Q(out_6));  // open: Qn, preset, en, reset
  D_Flip_Flop d_ff_4 (.clk(clock_1_out), .D(in_1), .Q(out_5));  // open: Qn, preset, en, reset
endmodule

module FullAdder (
  input  C,
  input  B,
  input  A,
  output S,
  output C_2
);

  wire and_1_out, and_2_out, and_3_out;

  ExactlyOne xor_1 (.out(S), .in1(C), .in2(B), .in3(A));
  and and_1 (and_1_out, C, B);
  and and_2 (and_2_out, C, A);
  and and_3 (and_3_out, B, A);
  or or_1 (C_2, and_1_out, and_2_out, and_3_out);
endmodule

module Somador (
  input  A0,
  input  B0,
  input  A1,
  input  B1,
  input  A2,
  input  B2,
  output S0,
  output S1,
  output S2,
  output C
);

  wire FA_c_2, HA_c;

  Carry HA (.in_1(A0), .in_2(B0), .S(S0), .C(HA_c));
  FullAdder FA (.C(HA_c), .B(A1), .A(B1), .S(S1), .C_2(FA_c_2));
  FullAdder FA_2 (.C(FA_c_2), .B(A2), .A(B2), .S(S2), .C_2(C));
endmodule

module Decoderr (
  input  C,
  input  B,
  input  A,
  output a_2,
  output b_2,
  output c_2,
  output d,
  output e,
  output f,
  output g
);

  wire and_1_out, and_2_out, and_3_out, and_4_out, and_5_out, and_6_out, and_7_out, and_8_out, and_9_out,
       and_10_out, and_11_out, and_12_out, and_13_out, and_14_out, and_15_out, and_16_out, not_1_out,
       not_2_out, not_3_out, not_4_out, not_5_out, not_6_out, not_7_out, not_8_out, not_9_out, not_10_out,
       not_11_out, not_12_out, not_13_out, not_14_out, not_15_out, not_16_out, not_17_out, not_18_out,
       not_19_out, not_20_out, not_21_out;

  not not_1 (not_1_out, C);
  not not_2 (not_2_out, A);
  not not_3 (not_3_out, B);
  not not_4 (not_4_out, A);
  not not_5 (not_5_out, B);
  not not_6 (not_6_out, C);
  not not_7 (not_7_out, A);
  not not_8 (not_8_out, C);
  not not_9 (not_9_out, A);
  not not_10 (not_10_out, B);
  not not_11 (not_11_out, C);
  not not_12 (not_12_out, A);
  not not_13 (not_13_out, A);
  not not_14 (not_14_out, B);
  not not_15 (not_15_out, A);
  not not_16 (not_16_out, B);
  not not_17 (not_17_out, A);
  not not_18 (not_18_out, C);
  not not_19 (not_19_out, B);
  not not_20 (not_20_out, A);
  and and_1 (and_1_out, not_1_out, not_2_out);
  and and_2 (and_2_out, C, A);
  not not_21 (not_21_out, C);
  and and_3 (and_3_out, not_3_out, not_4_out);
  and and_4 (and_4_out, B, A);
  or or_1 (c_2, not_5_out, A, C);
  and and_5 (and_5_out, not_6_out, not_7_out);
  and and_6 (and_6_out, not_8_out, B);
  and and_7 (and_7_out, B, not_9_out);
  and and_8 (and_8_out, C, not_10_out, A);
  and and_9 (and_9_out, not_11_out, not_12_out);
  and and_10 (and_10_out, B, not_13_out);
  and and_11 (and_11_out, not_14_out, not_15_out);
  and and_12 (and_12_out, C, not_16_out);
  and and_13 (and_13_out, C, not_17_out);
  and and_14 (and_14_out, not_18_out, B);
  and and_15 (and_15_out, C, not_19_out);
  and and_16 (and_16_out, C, not_20_out);
  or or_2 (a_2, and_1_out, B, and_2_out);
  or or_3 (b_2, not_21_out, and_3_out, and_4_out);
  or or_4 (d, and_5_out, and_6_out, and_7_out, and_8_out);
  or or_5 (e, and_9_out, and_10_out);
  or or_6 (f, and_11_out, and_12_out, and_13_out);
  or or_7 (g, and_14_out, and_15_out, and_16_out);
endmodule
