// Logisim project Exec_1.circ as structural Verilog: 1 circuit, main circuit main
module main (
  input  A,
  input  B,
  input  C,
  output S
);

  wire A_C_out, A_prime_B_C_out, B_C_prime_out, not_1_out, not_2_out;

  not not_1 (not_1_out, A);
  not not_2 (not_2_out, C);
  and A_C (A_C_out, A, C);
  and A_prime_B_C (A_prime_B_C_out, not_1_out, C, B);
  and B_C_prime (B_C_prime_out, B, not_2_out);
  or or_1 (S, A_C_out, A_prime_B_C_out, B_C_prime_out);
endmodule
